# Fritzing sketch Untitled Sketch (saved by Fritzing 0.9.3b)
breadboards: 1

parts:
  Part1 = Arduino Uno (Rev3)
  LED1 = LED - 5mm [color="Red (633nm)" package="5 mm [THT]"]
  R1 = Resistor [tolerance=±20% resistance=220 package=THT]

nets:
  N1: Part1.D13/SCK, LED1.cathode
  N2: Part1.GND, R1.Pin_1
  N3: LED1.anode, R1.Pin_0

// code stored in the sketch: Untitled.ino
#define LED_PIN 13

void setup()
{
    pinMode(LED_PIN, OUTPUT);
}

void loop()
{
    digitalWrite(LED_PIN, HIGH);
    delay(100);
    digitalWrite(LED_PIN, LOW);
    delay(900);
}
